// Logisim project 5 bit ALU.circ as structural Verilog: 5 circuits, main circuit 5 bit OR
module _5_bit_OR (
  input  [4:0] in_1,
  input  [4:0] in_2,
  output [4:0] out_3
);

  assign out_3 = in_1 | in_2;  // OR_Gate or_1, 5 bits wide

  // Notes on the sheet:
  //   A[4:0]
  //   B[4:0]
  //   O[4:0]
endmodule

module _5_Bit_XOR (
  input  [4:0] in_1,
  input  [4:0] in_2,
  output [4:0] out_3
);

  assign out_3 = in_1 ^ in_2;  // XOR_Gate xor_1, 5 bits wide
endmodule

module _1_bit_Register (
  input  in_1,
  input  in_2,
  input  in_3,
  output out_4
);

  wire multiplexer_1_out;

  Multiplexer multiplexer_1 (.in0(out_4), .in1(in_1), .out(multiplexer_1_out), .sel(in_2));  // open: en
  D_Flip_Flop d_ff_1 (.clk(in_3), .D(multiplexer_1_out), .Q(out_4));  // open: Qn, preset, en, reset
endmodule

module _5_Bit_ALU (
  input  [5:0] A_4_0,
  input  [5:0] B_4_0,
  input  [3:0] OP_3_0,
  output [4:0] R_4_0,
  output ZF
);

  wire [4:0] n5_bit_or_1_out_3, n5_bit_xor_1_out_3;

  _5_bit_OR u_5_bit_or_1 (.in_1(B_4_0[4:0]), .in_2(A_4_0[4:0]), .out_3(n5_bit_or_1_out_3));
  _5_Bit_XOR u_5_bit_xor_1 (.in_1(A_4_0[4:0]), .in_2(B_4_0[4:0]), .out_3(n5_bit_xor_1_out_3));
  Multiplexer #(.select(4), .width(5)) multiplexer_1 (
    .in0(n5_bit_or_1_out_3), .in1(n5_bit_xor_1_out_3), .out(R_4_0), .sel(OP_3_0));  // open: in2, in3, in4, in5, in6, in7, in8, in9, in10, in11, in12, in13, in14, in15, en
  nor nor_1 (ZF, R_4_0[0], R_4_0[1], R_4_0[2], R_4_0[3], R_4_0[4]);
  // Pins of 5 and 6 bits meet at B_4_0
  // Pins of 5 and 6 bits meet at A_4_0

  // Other names for the same wires on the sheet: A[5:0] = A_4_0; B[5:0] = B_4_0
endmodule

module _5_bit_register (
  input  [4:0] in_1,
  input  in_2,
  output [4:0] out_3
);

  wire clock_1_out;

  Clock clock_1 (.out(clock_1_out));
  _1_bit_Register u_1_bit_register_1 (.in_1(in_1[0]), .in_2(in_2), .out_4(out_3[0]), .in_3(clock_1_out));
  _1_bit_Register u_1_bit_register_2 (.in_1(in_1[1]), .in_2(in_2), .out_4(out_3[1]), .in_3(clock_1_out));
  _1_bit_Register u_1_bit_register_3 (.in_1(in_1[2]), .in_2(in_2), .out_4(out_3[2]), .in_3(clock_1_out));
  _1_bit_Register u_1_bit_register_4 (.in_1(in_1[3]), .in_2(in_2), .out_4(out_3[3]), .in_3(clock_1_out));
  _1_bit_Register u_1_bit_register_5 (.in_1(in_1[4]), .in_2(in_2), .out_4(out_3[4]), .in_3(clock_1_out));
endmodule
