// Logisim project OR.circ as structural Verilog: 3 circuits, main circuit 6 bit OR
module _6_bit_OR (
  input  [5:0] in_1,
  input  [5:0] in_2,
  output [5:0] out_3
);

  assign out_3 = in_1 | in_2;  // OR_Gate or_1, 6 bits wide

  // Notes on the sheet:
  //   A[5:0]
  //   B[5:0]
  //   O[5:0]
endmodule

module _6_Bit_XOR (
  input  [5:0] A_5_0,
  input  [5:0] B_5_0,
  output [5:0] O_5_0
);

  assign O_5_0 = A_5_0 ^ B_5_0;  // XOR_Gate xor_1, 6 bits wide
endmodule

module _6_Bit_ALU (
  input  [5:0] A_5_0,
  input  [5:0] B_5_0,
  input  [3:0] OP_3_0,
  output [5:0] R_5_0
);

  wire [5:0] n6_bit_or_1_out_3, n6_bit_xor_1_o_5_0;

  _6_bit_OR u_6_bit_or_1 (.in_1(B_5_0), .in_2(A_5_0), .out_3(n6_bit_or_1_out_3));
  _6_Bit_XOR u_6_bit_xor_1 (.A_5_0(A_5_0), .B_5_0(B_5_0), .O_5_0(n6_bit_xor_1_o_5_0));
  Multiplexer #(.select(4), .width(6)) multiplexer_1 (
    .in0(n6_bit_or_1_out_3), .in1(n6_bit_xor_1_o_5_0), .out(R_5_0), .sel(OP_3_0));  // open: in2, in3, in4, in5, in6, in7, in8, in9, in10, in11, in12, in13, in14, in15, en

  // Other names for the same wires on the sheet: A[5:0] = A_5_0; B[5:0] = B_5_0
endmodule
