// Logisim project Register Set.circ as structural Verilog: 9 circuits, main circuit 6 bit OR
module _6_bit_OR (
  input  [5:0] in_1,
  input  [5:0] in_2,
  output [5:0] out_3
);

  assign out_3 = in_1 | in_2;  // OR_Gate or_1, 6 bits wide

  // Notes on the sheet:
  //   A[5:0]
  //   B[5:0]
  //   O[5:0]
endmodule

module _6_Bit_XOR (
  input  [5:0] in_1,
  input  [5:0] in_2,
  output [5:0] out_3
);

  assign out_3 = in_1 ^ in_2;  // XOR_Gate xor_1, 6 bits wide

  // Notes on the sheet:
  //   A[5:0]
  //   B[5:0]
  //   O[5:0]
endmodule

module _1_bit_Register (
  input  in_1,
  input  in_2,
  input  in_3,
  output out_4
);

  wire multiplexer_1_out;

  Multiplexer multiplexer_1 (.in0(out_4), .in1(in_1), .out(multiplexer_1_out), .sel(in_2));  // open: en
  D_Flip_Flop d_ff_1 (.clk(in_3), .D(multiplexer_1_out), .Q(out_4));  // open: Qn, preset, en, reset
endmodule

module _6_Bit_ALU (
  input  [5:0] A_4_0,
  input  [5:0] B_4_0,
  input  [3:0] OP_3_0,
  output [5:0] out_4
);

  wire [5:0] n6_bit_or_1_out_3, n6_bit_xor_1_out_3, undriven;

  _6_Bit_XOR u_6_bit_xor_1 (.in_1(A_4_0), .in_2(B_4_0), .out_3(n6_bit_xor_1_out_3));
  _6_bit_OR u_6_bit_or_1 (.in_1(A_4_0), .in_2(B_4_0), .out_3(n6_bit_or_1_out_3));
  Multiplexer #(.select(4), .width(6)) multiplexer_1 (
    .in0(n6_bit_or_1_out_3), .in1(n6_bit_xor_1_out_3), .in2(undriven), .out(out_4), .sel(OP_3_0));  // open: in3, in4, in5, in6, in7, in8, in9, in10, in11, in12, in13, in14, in15, en

  // Other names for the same wires on the sheet: A[5:0] = A_4_0; B[5:0] = B_4_0

  // Notes on the sheet:
  //   R[5:0]
endmodule

module _6_bit_register (
  input  [5:0] in_1,
  input  in_2,
  input  in_3,
  output [5:0] out_4
);

  _1_bit_Register u_1_bit_register_1 (.in_1(in_1[0]), .in_2(in_2), .out_4(out_4[0]), .in_3(in_3));
  _1_bit_Register u_1_bit_register_2 (.in_1(in_1[1]), .in_2(in_2), .out_4(out_4[1]), .in_3(in_3));
  _1_bit_Register u_1_bit_register_3 (.in_1(in_1[2]), .in_2(in_2), .out_4(out_4[2]), .in_3(in_3));
  _1_bit_Register u_1_bit_register_4 (.in_1(in_1[3]), .in_2(in_2), .out_4(out_4[3]), .in_3(in_3));
  _1_bit_Register u_1_bit_register_5 (.in_1(in_1[4]), .in_2(in_2), .out_4(out_4[4]), .in_3(in_3));
  _1_bit_Register u_1_bit_register_6 (.in_1(in_1[5]), .in_2(in_2), .out_4(out_4[5]), .in_3(in_3));
endmodule

module Register_Set (
  input  [1:0] Ra,
  input  REG_EN,
  input  [1:0] Sel_1_0,
  input  [5:0] in_4,
  input  Clock,
  input  [1:0] Rb_1_0,
  output [5:0] A_5_0,
  output [5:0] B_5_0
);

  wire decoder_1_out0, decoder_1_out1, decoder_1_out2;
  wire [5:0] n6_bit_register_1_out_4, n6_bit_register_2_out_4, n6_bit_register_3_out_4;

  Decoder #(.select(2)) decoder_1 (
    .out0(decoder_1_out0), .out1(decoder_1_out1), .out2(decoder_1_out2), .sel(Sel_1_0), .en(REG_EN));  // open: out3
  _6_bit_register u_6_bit_register_1 (
    .in_1(in_4), .in_2(decoder_1_out0), .in_3(Clock), .out_4(n6_bit_register_1_out_4));
  _6_bit_register u_6_bit_register_2 (
    .in_1(in_4), .in_2(decoder_1_out1), .in_3(Clock), .out_4(n6_bit_register_2_out_4));
  _6_bit_register u_6_bit_register_3 (
    .in_1(in_4), .in_2(decoder_1_out2), .in_3(Clock), .out_4(n6_bit_register_3_out_4));
  Multiplexer #(.select(2), .width(6)) multiplexer_1 (
    .in0(n6_bit_register_1_out_4), .in1(n6_bit_register_2_out_4), .in2(n6_bit_register_3_out_4), .out(A_5_0),
    .sel(Ra));  // open: in3, en
  Multiplexer #(.select(2), .width(6)) multiplexer_2 (
    .in0(n6_bit_register_1_out_4), .in1(n6_bit_register_2_out_4), .in2(n6_bit_register_3_out_4), .out(B_5_0),
    .sel(Rb_1_0));  // open: in3, en

  // Notes on the sheet:
  //   wrd[5:0]
endmodule

module _1x1_SRam (
  input  Read_select_1,
  input  Read_select_2,
  input  Write_Data,
  input  Write_select,
  input  clock,
  output Read_data_1,
  output Read_data_2
);

  wire d_ff_1_q, multiplexer_1_out;

  Multiplexer #(.enable("false")) multiplexer_1 (
    .in0(d_ff_1_q), .in1(Write_Data), .out(multiplexer_1_out), .sel(Write_select));
  D_Flip_Flop d_ff_1 (.clk(clock), .D(multiplexer_1_out), .Q(d_ff_1_q));  // open: Qn, preset, en, reset
  and and_1 (Read_data_1, Read_select_1, d_ff_1_q);
  and and_2 (Read_data_2, Read_select_2, d_ff_1_q);
endmodule

module _1x4_Sram (
  input  Read_select_1,
  input  Read_select_2,
  input  Write_Select,
  input  [3:0] Write_Data,
  input  Clock,
  output [3:0] out_6,
  output [3:0] out_7
);

  _1x1_SRam u_1x1_sram_1 (
    .Read_select_1(Read_select_1), .Read_select_2(Read_select_2), .Write_Data(Write_Data[0]),
    .Write_select(Write_Select), .clock(Clock), .Read_data_1(out_6[0]), .Read_data_2(out_7[0]));
  _1x1_SRam u_1x1_sram_2 (
    .Read_select_1(Read_select_1), .Read_select_2(Read_select_2), .Write_Data(Write_Data[1]),
    .Write_select(Write_Select), .clock(Clock), .Read_data_1(out_6[1]), .Read_data_2(out_7[1]));
  _1x1_SRam u_1x1_sram_3 (
    .Read_select_1(Read_select_1), .Read_select_2(Read_select_2), .Write_Data(Write_Data[2]),
    .Write_select(Write_Select), .clock(Clock), .Read_data_1(out_6[2]), .Read_data_2(out_7[2]));
  _1x1_SRam u_1x1_sram_4 (
    .Read_select_1(Read_select_1), .Read_select_2(Read_select_2), .Write_Data(Write_Data[3]),
    .Write_select(Write_Select), .clock(Clock), .Read_data_1(out_6[3]), .Read_data_2(out_7[3]));

  // Notes on the sheet:
  //   Read Data 1
  //   Read Data 2
endmodule

module _1x16_SRam (
  input  Read_Select_1,
  input  Read_Select_2,
  input  Write_Select,
  input  Clock,
  input  [15:0] in_5,
  output [15:0] out_6,
  output [15:0] out_7
);

  _1x4_Sram u_1x4_sram_1 (
    .Read_select_1(Read_Select_1), .Read_select_2(Read_Select_2), .Write_Select(Write_Select),
    .Write_Data(in_5[15:12]), .Clock(Clock), .out_6(out_6[15:12]), .out_7(out_7[15:12]));
  _1x4_Sram u_1x4_sram_2 (
    .Read_select_1(Read_Select_1), .Read_select_2(Read_Select_2), .Write_Select(Write_Select),
    .Write_Data(in_5[11:8]), .Clock(Clock), .out_6(out_6[11:8]), .out_7(out_7[11:8]));
  _1x4_Sram u_1x4_sram_3 (
    .Read_select_1(Read_Select_1), .Read_select_2(Read_Select_2), .Write_Select(Write_Select),
    .Write_Data(in_5[7:4]), .Clock(Clock), .out_6(out_6[7:4]), .out_7(out_7[7:4]));
  _1x4_Sram u_1x4_sram_4 (
    .Read_select_1(Read_Select_1), .Read_select_2(Read_Select_2), .Write_Select(Write_Select),
    .Write_Data(in_5[3:0]), .Clock(Clock), .out_6(out_6[3:0]), .out_7(out_7[3:0]));

  // Notes on the sheet:
  //   Write Data
  //   Read Data 1
  //   Read data 2
endmodule
