// Logisim project XOR.circ as structural Verilog
module _5_bit_OR (
  input  [4:0] in_1,
  input  [4:0] in_2,
  output [4:0] out_3
);

  assign out_3 = in_1 | in_2;  // OR_Gate or_1, 5 bits wide

  // Notes on the sheet:
  //   A[4:0]
  //   B[4:0]
  //   O[4:0]
endmodule
